# Fritzing sketch RPiLarm (saved by Fritzing 0.9.2b)
circuit board: 3.61449cm x 4.51038cm

parts:
  1 = SWITCH-MOMENTARY-2 [package=tactile-pth]
  G_O_V+ = female pin header, 3 pins [form="♀ (female)"]
  2 = SWITCH-MOMENTARY-2 [package=tactile-pth]
  3 = SWITCH-MOMENTARY-2 [package=tactile-pth]
  4 = SWITCH-MOMENTARY-2 [package=tactile-pth]
  5 = SWITCH-MOMENTARY-2 [package=tactile-pth]
  6 = SWITCH-MOMENTARY-2 [package=tactile-pth]
  7 = SWITCH-MOMENTARY-2 [package=tactile-pth]
  8 = SWITCH-MOMENTARY-2 [package=tactile-pth]
  9 = SWITCH-MOMENTARY-2 [package=tactile-pth]
  DEL = SWITCH-MOMENTARY-2 [package=tactile-pth]
  0 = SWITCH-MOMENTARY-2 [package=tactile-pth]
  (c)Z_Igielman_& = Buzzer 12mm [package=buzzer-12mm-ns]
  Raspberry_Pi1 = Raspberry Pi B rev2
  J_Blumenow = LED - 3mm [color="Red (633nm)" package="3 mm [THT]"]
  R1 = Resistor [tolerance=±5% resistance=220 package=THT]
  R2 = Resistor [tolerance=±5% resistance=220 package=THT]

nets:
  N1: 1.1, Raspberry_Pi1.GPIO_3
  N2: 1.2, G_O_V+.pin1, 2.2, 3.2, 4.2, 5.2, 6.2, 7.2, 8.2, 9.2, DEL.2, 0.2, (c)Z_Igielman_&.2, Raspberry_Pi1.GND, J_Blumenow.cathode
  N3: G_O_V+.pin2, Raspberry_Pi1.GPIO_14
  N4: G_O_V+.pin3, Raspberry_Pi1.5V
  N5: 2.1, Raspberry_Pi1.GPIO_27
  N6: 3.1, Raspberry_Pi1.GPIO_7
  N7: 4.1, Raspberry_Pi1.GPIO_4
  N8: 5.1, Raspberry_Pi1.GPIO_22
  N9: 6.1, Raspberry_Pi1.GPIO_8
  N10: 7.1, Raspberry_Pi1.GPIO_17
  N11: 8.1, Raspberry_Pi1.GPIO_10
  N12: 9.1, Raspberry_Pi1.GPIO_25
  N13: DEL.1, Raspberry_Pi1.GPIO_11
  N14: 0.1, Raspberry_Pi1.GPIO_9
  N15: (c)Z_Igielman_&.1, R2.Pin_1
  N16: Raspberry_Pi1.GPIO_15, R2.Pin_0
  N17: Raspberry_Pi1.GPIO_18, R1.Pin_1
  N18: J_Blumenow.anode, R1.Pin_0

notes:
  RPiLarm
